# Fritzing sketch esp8266_rele_v5.2 (saved by Fritzing 0.9.3b)
circuit board: 5cm x 3.47545cm
breadboards: 1

parts:
  C1 = Electrolytic Capacitor [capacitance=10µF voltage=50V package="100 mil [THT, electrolytic]"]
  K1 = OMRON PCB Power Relay – G5LE [part_number="G5LE-1\n" package=THT]
  Q1 = NPN-Transistor [package="TO92 [THT]"]
  R6 = Resistor [tolerance=±5% resistance=330 package=THT]
  R4 = Resistor [tolerance=±5% resistance=2.7k package=THT]
  D2 = Diode [package=diode-1n4001]
  R5 = Resistor [tolerance=±5% resistance=47k package=THT]
  U1 = Voltage Regulator LM1117 [package=sot223]
  J3 = female pin header, 4 pins [form="♀ (female)"]
  J4 = female pin header, 4 pins [form="♀ (female)"]
  S1 = Pushbutton [package="[THT]"]
  R3 = Resistor [tolerance=±5% resistance=2.7k package=THT]
  ESP8266 = double row female pin header, 8 pins [form="♀ (female)"]
  R1 = Resistor [tolerance=±5% resistance=2.7k package=THT]
  R2 = Resistor [tolerance=±5% resistance=2.7k package=THT]
  L1 = LED - 3mm [color="Green (560nm)" package="3 mm [THT]"]
  D1 = Diode [package=diode-1n4001]
  J9 = Screw terminal - 2 pins [package=THT]
  J10 = female pin header, 2 pins [form="♀ (female)"]
  J8 = screw terminal, 3 pins
  J11 = female pin header, 2 pins [form="♀ (female)"]

nets:
  N1: C1.-, Q1.E, R5.Pin_0, U1.ADJ, J4.pin4, S1.Pin_1, S1.Pin_2, ESP8266.pin8, J10.pin1
  N2: C1.+, U1.OUT, J3.pin1, J3.pin3, R3.Pin_1, ESP8266.pin2, ESP8266.pin4, R1.Pin_1, R2.Pin_1
  N3: K1.A, J8.pin3
  N4: K1.COIL1, Q1.C, L1.cathode, D1.A
  N5: K1.C, J8.pin2
  N6: K1.COIL2, R6.Pin_1, U1.IN, D1.C, J10.pin2
  N7: K1.B, J8.pin1
  N8: Q1.B, R4.Pin_0, R5.Pin_1
  N9: R6.Pin_0, L1.anode
  N10: R4.Pin_1, D2.C
  N11: D2.A, J4.pin3, ESP8266.pin5
  N12: J3.pin2, ESP8266.pin3, R1.Pin_0
  N13: J3.pin4, ESP8266.pin1
  N14: J4.pin1, ESP8266.pin7, R2.Pin_0
  N15: J4.pin2, ESP8266.pin6
  N16: S1.Pin_3, S1.Pin_4, R3.Pin_0
  N17: J9.pin1, J11.pin1
  N18: J9.pin2, J11.pin2

notes:
  ESP8266 - Pinos:
  Gnd - GPIO2 - GPIO0 - RX
  TX - CH_PD - RESET - VCC
  = LISTA DE MATERIAIS ====
  Reg. Tensao ------------------
  U1= AMS1117 (3.3V)
  - Resistors ----------------------
  R1 = 2.7k (pull up 3.3v)
  R2 = 2.7k (pull up 3.3v)
  R3 = 2.7k (pull up 3.3v)
  R4 = 2.7K (pull up 3.3v)
  R5 = 47 K (pull up 5.0v)
  R6 = 330R (led)
  - Transistors -------------------
  Q1 = BC548/BC549
  - Capacitor ----------------------
  C1 = 10uF
  - Diodos -------------------------
  D1 = 1N4007
  D2 = 1N4007
  L1 = LED 3mm - Verde
  - Rele -----------------------------
  K1 = Rele 5V
  - Outros -------------------------
  J1 = Borne 3 vias
  J2 = Power Jack P4
  J3 = Nao precisa (apenas furos)
  J4 = Nao precisa (apenas furos)
  S1= Push Button
  5v
  Tamanho 60mm x 35mm
  Wifi Relay
  +
  -
  Formula para calcular a resistencia da base:
  R = ((Vin - 0,6) * HEF)) / I_rele
  Ex.:
  R = ((3.3v - 0,6V) * 100) / 0,08A (=>80mA)
  R = 3.375 ohms
  Vou usar 2.4K porque tem um diodo (D2) em serie que vai derrubar mais 0,6V.
  NF
  NA
  C
  jun/2016
  JRPERIN
  3.3v
  ac
  Relay Control
  wifi
  JRPerin
  v1.0
  AC
