# Fritzing sketch esp8266_rele (saved by Fritzing 0.9.3b)
circuit board: 2.2cm x 1.4cm
circuit board: 8.5cm x 3.5cm
breadboards: 1

parts:
  10uF = Electrolytic Capacitor [capacitance=10µF voltage=50V package="100 mil [THT, electrolytic]"]  # not connected
  U1 = Voltage Regulator LM1117 [package=sot223]
  K1 = OMRON PCB Power Relay – G5LE [part_number="G5LE-1\n" package=THT]
  D2 = Diode [package=diode-1n4001]
  Q1 = NPN-Transistor [package="TO92 [THT]"]
  R1 = Resistor [tolerance=±5% resistance=220 package=THT]
  J17 = Power Jack [package=power_jack_slot]
  LED1 = LED - 5mm [color="Red (633nm)" package="5 mm [THT]"]
  J18 = screw terminal, 3 pins
  J19 = female pin header, 2 pins [form="♀ (female)"]
  J20 = Generic double row female header - 8 pins [form="♀ (female)" package=THT]
  R2 = Resistor [tolerance=±5% resistance=220 package=THT]
  S1 = Pushbutton [package="[THT]"]
  R3 = Resistor [tolerance=±5% resistance=220 package=THT]

nets:
  N1: U1.ADJ, Q1.E, J17.GND, J20.pin8, S1.Pin_1, S1.Pin_2
  N2: U1.OUT, J20.pin4, R3.Pin_1
  N3: U1.IN, K1.COIL2, D2.C, R1.Pin_1, J17.PWR, LED1.anode
  N4: K1.A, J18.pin3
  N5: K1.COIL1, D2.A, Q1.C, LED1.cathode
  N6: K1.C, J18.pin2
  N7: K1.B, J18.pin1
  N8: Q1.B, R2.Pin_0
  N9: J19.pin1, J20.pin7
  N10: J19.pin2, R2.Pin_1
  N11: J20.pin3, S1.Pin_3, S1.Pin_4, R3.Pin_0

notes:
  ESP8266
  ESP8266 - Pinos:
  Gnd - GPIO2 - GPIO0 - RX
  TX - CH_PD - RESET - VCC
  5v
  Tamanho 85mm x 35 mm
  PerinoWifi

custom parts:
  Generic double row female header - 8 pins: Generic double row female header
