# Fritzing sketch esp8266_rele_v3 (saved by Fritzing 0.9.3b)
circuit board: 7.5cm x 3.5cm
breadboards: 1

parts:
  10uF = Electrolytic Capacitor [capacitance=10µF voltage=50V package="100 mil [THT, electrolytic]"]
  K1 = OMRON PCB Power Relay – G5LE [part_number="G5LE-1\n" package=THT]
  D1 = Diode [package=diode-1n4001]
  Q1 = NPN-Transistor [package="TO92 [THT]"]
  R1 = Resistor [tolerance=±5% resistance=220 package=THT]
  J2 = Power Jack [package=power_jack_slot]
  LED1 = LED - 5mm [color="Green (560nm)" package="5 mm [THT]"]
  J1 = screw terminal, 3 pins
  ESP8266 = Generic double row female header - 8 pins [form="♀ (female)" package=THT]
  R2 = Resistor [tolerance=±5% resistance=220 package=THT]
  S1 = Pushbutton [package="[THT]"]
  R3 = Resistor [tolerance=±5% resistance=220 package=THT]
  J22 = female pin header, 4 pins [form="♀ (female)"]
  J23 = female pin header, 4 pins [form="♀ (female)"]
  D2 = Diode [package=diode-1n4001]
  R4 = Resistor [tolerance=±5% resistance=220 package=THT]
  U1 = Voltage Regulator LM1117 [package=sot223]

nets:
  N1: 10uF.-, Q1.E, J2.GND, ESP8266.pin8, S1.Pin_3, S1.Pin_4, J22.pin4, R4.Pin_0, U1.ADJ
  N2: 10uF.+, ESP8266.pin2, ESP8266.pin3, ESP8266.pin4, S1.Pin_1, S1.Pin_2, R3.Pin_1, J23.pin1, J23.pin2, J23.pin3, U1.OUT
  N3: K1.A, J1.pin3
  N4: K1.COIL1, D1.A, Q1.C, LED1.cathode
  N5: K1.C, J1.pin2
  N6: K1.COIL2, D1.C, R1.Pin_1, J2.PWR, U1.IN
  N7: K1.B, J1.pin1
  N8: Q1.B, R2.Pin_0, R4.Pin_1
  N9: R1.Pin_0, LED1.anode
  N10: ESP8266.pin1, J23.pin4
  N11: ESP8266.pin5, J22.pin3
  N12: ESP8266.pin6, J22.pin2
  N13: ESP8266.pin7, J22.pin1, D2.A
  N14: R2.Pin_1, D2.C

notes:
  ESP8266 - Pinos:
  Gnd - GPIO2 - GPIO0 - RX
  TX - CH_PD - RESET - VCC
  R1= 330R
  R2= 2.4K
  R3= 2.4K
  R4= 47K
  Q1= BC548/BC549
  D1= 1N4007
  D2= 1N4007
  K1= Rele 5v
  J1 = Borne 3 vias
  J2 = Power Jack
  5v
  Tamanho 80mm x 35 mm
  ESP8266
  Relay Wifi
  +
  -
  Formula para calcular a resistencia da base:
  R = ((Vin - 0,6) * HEF)) / I_rele
  Ex.:
  R = ((3.3v - 0,6V) * 100) / 0,08A (=>80mA)
  R = 3.375 ohms
  Vou usar 2.4K porque tem um diodo (D2) em serie que vai derrubar mais 0,6V.
  NF
  NA
  C
  jun/2016
  JRPERIN

custom parts:
  Generic double row female header - 8 pins: Generic double row female header
