# Fritzing sketch esp8266_rele_v5 (saved by Fritzing 0.9.3b)
circuit board: 6.5cm x 3.5cm
breadboards: 1

parts:
  10uF = Electrolytic Capacitor [capacitance=10µF voltage=50V package="100 mil [THT, electrolytic]"]
  K1 = OMRON PCB Power Relay – G5LE [part_number="G5LE-1\n" package=THT]
  D1 = Diode [package=diode-1n4001]
  Q1 = NPN-Transistor [package="TO92 [THT]"]
  R1 = Resistor [tolerance=±5% resistance=330 package=THT]
  J2 = Power Jack [package=power_jack_slot]
  LED1 = LED - 5mm [color="Green (560nm)" package="5 mm [THT]"]
  J1 = screw terminal, 3 pins
  R2 = Resistor [tolerance=±5% resistance=2.4k package=THT]
  D2 = Diode [package=diode-1n4001]
  R5 = Resistor [tolerance=±5% resistance=47k package=THT]
  U1 = Voltage Regulator LM1117 [package=sot223]
  J3 = female pin header, 4 pins [form="♀ (female)"]
  J4 = female pin header, 4 pins [form="♀ (female)"]
  S1 = Pushbutton [package="[THT]"]
  R3 = Resistor [tolerance=±5% resistance=2.4k package=THT]
  ESP8266 = double row female pin header, 8 pins [form="♀ (female)"]
  R4 = Resistor [tolerance=±5% resistance=2.4k package=THT]
  R6 = Resistor [tolerance=±5% resistance=2.7k package=THT]

nets:
  N1: 10uF.-, Q1.E, J2.GND, R5.Pin_0, U1.ADJ, J4.pin4, S1.Pin_1, S1.Pin_2, ESP8266.pin8
  N2: 10uF.+, U1.OUT, J3.pin1, J3.pin3, R3.Pin_1, ESP8266.pin2, ESP8266.pin4, R4.Pin_1, R6.Pin_1
  N3: K1.A, J1.pin3
  N4: K1.COIL1, D1.A, Q1.C, LED1.cathode
  N5: K1.C, J1.pin2
  N6: K1.COIL2, D1.C, R1.Pin_1, J2.PWR, U1.IN
  N7: K1.B, J1.pin1
  N8: Q1.B, R2.Pin_0, R5.Pin_1
  N9: R1.Pin_0, LED1.anode
  N10: R2.Pin_1, D2.C
  N11: D2.A, J4.pin3, ESP8266.pin5
  N12: J3.pin2, ESP8266.pin3, R4.Pin_0
  N13: J3.pin4, ESP8266.pin1
  N14: J4.pin1, ESP8266.pin7, R6.Pin_0
  N15: J4.pin2, ESP8266.pin6
  N16: S1.Pin_3, S1.Pin_4, R3.Pin_0

notes:
  ESP8266 - Pinos:
  Gnd - GPIO2 - GPIO0 - RX
  TX - CH_PD - RESET - VCC
  U1= AMS1117 (3.3V)
  R1= 330R
  R2= 2.4K
  R3= 2.4K (pull down 3.3v)
  R4= 2.4K (pull down 3.3v)
  R5= 47K (pull down 5v)
  Q1= BC548/BC549
  D1= 1N4007
  D2= 1N4007
  K1= Rele 5V
  J1 = Borne 3 vias
  J2 = Power Jack P4
  S1= Push Button
  5v
  Tamanho 65mm x 35 mm
  Wifi Relay
  +
  -
  Formula para calcular a resistencia da base:
  R = ((Vin - 0,6) * HEF)) / I_rele
  Ex.:
  R = ((3.3v - 0,6V) * 100) / 0,08A (=>80mA)
  R = 3.375 ohms
  Vou usar 2.4K porque tem um diodo (D2) em serie que vai derrubar mais 0,6V.
  NF
  NA
  C
  jun/2016
  JRPERIN
  3.3v
